# Fritzing sketch influunt (saved by Fritzing 0.9.3b)
breadboards: 1

parts:
  Part1 = Arduino Mega 2560 (Rev3)
  R1 = Resistor [tolerance=±5% resistance=220 package=THT]
  DP1 = Pushbutton [package="[THT]"]
  R2 = Resistor [tolerance=±5% resistance=220 package=THT]
  R3 = Resistor [tolerance=±5% resistance=220 package=THT]
  R4 = Resistor [tolerance=±5% resistance=220 package=THT]
  R5 = Resistor [tolerance=±5% resistance=220 package=THT]
  R6 = Resistor [tolerance=±5% resistance=220 package=THT]
  R7 = Resistor [tolerance=±5% resistance=220 package=THT]
  R8 = Resistor [tolerance=±5% resistance=220 package=THT]
  DV1 = Pushbutton [package="[THT]"]
  Verdes_Conflitantes = Pushbutton [package="[THT]"]
  Falha_G1_Apagado = Pushbutton [package="[THT]"]
  Remoção_G1_Apagado = Pushbutton [package="[THT]"]
  DP1_Acionamento_Direto = Pushbutton [package="[THT]"]
  Falha_CPU = Pushbutton [package="[THT]"]
  Alarme_Abertura_de_Porta = Pushbutton [package="[THT]"]
  R9 = Resistor [tolerance=±5% resistance=220 package=THT]
  R10 = Resistor [tolerance=±5% resistance=220 package=THT]
  R11 = Resistor [tolerance=±5% resistance=220 package=THT]
  R12 = Resistor [tolerance=±5% resistance=220 package=THT]
  R13 = Resistor [tolerance=±5% resistance=220 package=THT]
  R14 = Resistor [tolerance=±5% resistance=220 package=THT]
  R15 = Resistor [tolerance=±5% resistance=220 package=THT]
  R16 = Resistor [tolerance=±5% resistance=220 package=THT]
  Reservado_Novo_Evento_1 = Pushbutton [package="[THT]"]
  Troca_de_Estágio_(Manual) = Pushbutton [package="[THT]"]
  Reservado_Novo_Evento_3 = Pushbutton [package="[THT]"]
  Reservado_Novo_Evento_2 = Pushbutton [package="[THT]"]
  Reservado_Novo_Evento_7 = Pushbutton [package="[THT]"]
  Reservado_Novo_Evento_6 = Pushbutton [package="[THT]"]
  Reservado_Novo_Evento_4 = Pushbutton [package="[THT]"]
  Reservado_Novo_Evento_5 = Pushbutton [package="[THT]"]
  Part2 = 24 NeoPixel Ring [part_number=1586]
  LED_Manual_Ativo = LED - 5mm [color="Red (633nm)" package="5 mm [THT]"]
  Modo_Manual = SPST Switch [package=switche-dpdt]
  R17 = Resistor [tolerance=±5% resistance=330 package=THT]

nets:
  GND: Part1.GND, R1.Pin_0, R2.Pin_0, R3.Pin_0, R4.Pin_0, R5.Pin_0, R6.Pin_0, R7.Pin_0, R8.Pin_0, Part2.GND, Modo_Manual.O, R17.Pin_0
  5V: Part1.5V, DP1.Pin_4, DV1.Pin_4, Verdes_Conflitantes.Pin_4, Falha_G1_Apagado.Pin_4, Remoção_G1_Apagado.Pin_4, DP1_Acionamento_Direto.Pin_4, Falha_CPU.Pin_4, Alarme_Abertura_de_Porta.Pin_4, Reservado_Novo_Evento_1.Pin_3, Reservado_Novo_Evento_1.Pin_4, Troca_de_Estágio_(Manual).Pin_3, Reservado_Novo_Evento_3.Pin_3, Reservado_Novo_Evento_2.Pin_3, Reservado_Novo_Evento_7.Pin_3, Reservado_Novo_Evento_6.Pin_3, Reservado_Novo_Evento_4.Pin_3, Reservado_Novo_Evento_5.Pin_3, Part2.VDD, Modo_Manual.S
  N1: Part1.D5_PWM, LED_Manual_Ativo.anode
  N2: Part1.D6_PWM, Modo_Manual.P
  N3: Part1.D7_PWM, Part2.IN
  N4: Part1.D22, DP1.Pin_1, DP1.Pin_2
  N5: Part1.D24, R7.Pin_1, DV1.Pin_1, DV1.Pin_2
  N6: Part1.D26, R6.Pin_1, Verdes_Conflitantes.Pin_1, Verdes_Conflitantes.Pin_2
  N7: Part1.D28, R5.Pin_1, Falha_G1_Apagado.Pin_1, Falha_G1_Apagado.Pin_2
  N8: Part1.D30, R4.Pin_1, Remoção_G1_Apagado.Pin_1, Remoção_G1_Apagado.Pin_2
  N9: Part1.D32, R3.Pin_1, DP1_Acionamento_Direto.Pin_1, DP1_Acionamento_Direto.Pin_2
  N10: Part1.D34, R2.Pin_1, Falha_CPU.Pin_1, Falha_CPU.Pin_2
  N11: Part1.D36, R1.Pin_1, Alarme_Abertura_de_Porta.Pin_1, Alarme_Abertura_de_Porta.Pin_2
  N12: Part1.D38, R13.Pin_1, Troca_de_Estágio_(Manual).Pin_1, Troca_de_Estágio_(Manual).Pin_2
  N13: Part1.D40, R14.Pin_1, Reservado_Novo_Evento_1.Pin_1, Reservado_Novo_Evento_1.Pin_2
  N14: Part1.D42, R16.Pin_1, Reservado_Novo_Evento_2.Pin_1, Reservado_Novo_Evento_2.Pin_2
  N15: Part1.D44, R15.Pin_1, Reservado_Novo_Evento_3.Pin_1, Reservado_Novo_Evento_3.Pin_2
  N16: Part1.D46, R11.Pin_1, Reservado_Novo_Evento_4.Pin_1, Reservado_Novo_Evento_4.Pin_2
  N17: Part1.D48, R12.Pin_1, Reservado_Novo_Evento_5.Pin_1, Reservado_Novo_Evento_5.Pin_2
  N18: Part1.D50, R9.Pin_1, Reservado_Novo_Evento_6.Pin_1, Reservado_Novo_Evento_6.Pin_2
  N19: Part1.D52, R10.Pin_1, Reservado_Novo_Evento_7.Pin_1, Reservado_Novo_Evento_7.Pin_2
  N20: R9.Pin_0, R10.Pin_0, R11.Pin_0, R12.Pin_0, R13.Pin_0, R14.Pin_0, R15.Pin_0, R16.Pin_0
  N21: LED_Manual_Ativo.cathode, R17.Pin_1

custom parts:
  24 NeoPixel Ring: 24 ultra bright smart LED NeoPixels are arranged in a circle with 2.6" (66mm) outer diameter. The rings are 'chainable' - connect the output pin of one to the input pin of another. Use only one microcontroller pin to control as many as you can chain together! Each LED is addressable as the driver chip is inside the LED. Each one has ~18mA constant current drive so the color will be very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
